# Fritzing sketch open-aquarium (saved by Fritzing 0.9.4)
breadboards: 1

parts:
  Part1 = Arduino Mega 2560 (Rev3)
  LED1 = LED - 5mm [color="Red (633nm)" package="5 mm [THT]"]
  R1 = Resistor [tolerance=±5% resistance=470 package="2010 [SMD]"]
  DHT2 = DHT22 Humidity and Temperature Sensor
  R4 = Resistor [tolerance=±5% resistance=10k package="0805 [SMD]"]
  R5 = Rotary Potentiometer (Large) [maximum_resistance=100kΩ package=THT]

nets:
  N1: Part1.D13_PWM, R1.Pin_0
  5V: Part1.5V, DHT2.VDD, R4.Pin_0, R5.leg2
  GND: Part1.GND, LED1.cathode, DHT2.GND, R5.wiper
  N2: Part1.D2_PWM, DHT2.DATA, R4.Pin_1
  N3: Part1.D3_PWM, R5.leg1
  N4: LED1.anode, R1.Pin_1

notes:
  Potentiometer Illustration:
  Photocell module
  Terminal 1: DO
  Terminal 2: GND
  Terminal 3: VCC

// code stored in the sketch: Untitled2.ino
void setup()
{
  Serial.begin(9600);
  pinMode(13, OUTPUT);
}

void loop()
{
  
  Serial.print("DATA ");
  digitalWrite(13, HIGH);
  delay(1000); // Wait for 1000 millisecond(s)
  // turn the LED off by making the voltage LOW
  digitalWrite(13, LOW);
  delay(1000); // Wait for 1000 millisecond(s)
}
